# Fritzing sketch BMP085 Test Schematic (saved by Fritzing 0.9.2b)
breadboards: 1

parts:
  U1 = atmega328 [package=dip]
  C1 = Electrolytic Capacitor [capacitance=10μF package="0605 [SMD, electrolytic]"]  # not connected
  C2 = Ceramic Capacitor [capacitance=100nF package="200 mil [THT, multilayer]"]
  C3 = Ceramic Capacitor [capacitance=100nF package="100 mil [THT, multilayer]"]
  XTAL1 = Crystal [frequency="16 Mhz" package=SMD]
  R1 = Resistor [tolerance=±5% resistance=2k package="0805 [SMD]"]
  R2 = Resistor [tolerance=±5% resistance=2k package="0603 [SMD]"]
  Part1 = Barometric Pressure Sensor - BMP085 Breakout

nets:
  N1: U1.A4, Part1.GND
  N2: U1.A5, Part1.EOC
  N3: C2.0, XTAL1.pin_1
  N4: C2.1, C3.0, R1.Pin_1, Part1.SDA
  N5: C3.1, XTAL1.pin_0
  N6: R1.Pin_0, R2.Pin_1, Part1.VCC
